# Fritzing sketch Esquemаtico Projetor (saved by Fritzing 0.9.3b)
breadboards: 1

parts:
  HLK-PM1 = HLK-PM01
  U1 = ESP32-38PinWide [part_number=ESP32-38PinWide]
  Mod1 = KY-019 5V Relay Module [package="Breakout board"]
  LED1 = LEDs [package=led10mm]
  Power_plug1 = Power plug

nets:
  N1: HLK-PM1.AC#0, Mod1.Common, Power_plug1.GND
  N2: HLK-PM1.AC#1, LED1.A, Power_plug1.VCC
  N3: HLK-PM1.-Vo, U1.GPIO11, Mod1.-
  N4: HLK-PM1.+Vo, U1.VIN, Mod1.+
  N5: U1.GPIO23, Mod1.S
  N6: Mod1.NO, LED1.C

custom parts:
  ESP32-38PinWide: Generic 38-Pin ESP32 with wide format (only access to one side of pins on a breadboard) based on Stephen Lilley's HiLetgo ESP-WROOM-32 ESP32 ESP-32S Development Board.
  KY-019 5V Relay Module: KY-019 5V Relay module, used to control AC circuits.
  LEDs: LEDs Standard schematic elements and footprints for 5mm, 3mm, 1206, and 0603 sized LEDs. 5mm - Spark Fun Electronics SKU : COM-00529 (and others)
