# Fritzing sketch Projetor (saved by Fritzing 0.9.3b)
breadboards: 1

parts:
  U1 = ESP32-38PinWide [part_number=ESP32-38PinWide]
  Mod1 = KY-019 5V Relay Module [package="Breakout board"]
  M1 = AC-05-03
  LED1 = smd LED [color="Red (633nm)" package="0603 [SMD]"]
  VCC1 = Battery

nets:
  N1: U1.GPIO11, Mod1.-, M1.pin_4
  N2: U1.VIN, Mod1.+, M1.pin_3
  N3: U1.GPIO4, Mod1.S
  N4: Mod1.Common, M1.pin_2, VCC1.-
  N5: Mod1.NO, LED1.cathode
  N6: M1.pin_1, LED1.anode, VCC1.+

custom parts:
  ESP32-38PinWide: Generic 38-Pin ESP32 with wide format (only access to one side of pins on a breadboard) based on Stephen Lilley's HiLetgo ESP-WROOM-32 ESP32 ESP-32S Development Board.
  KY-019 5V Relay Module: KY-019 5V Relay module, used to control AC circuits.
  AC-05-03: AC-DC 220V to 5V Step-Down Power Supply Module
